# Fritzing sketch BigRobotTracker (saved by Fritzing 0.9.3b)
breadboards: 1

parts:
  U1 = 2-Channel 5v Relay Shield [package=relay-2ch5v10a]
  U2 = 2-Channel 5v Relay Shield [package=relay-2ch5v10a]
  Componente1 = Arduino Micro (Rev3)
  BAT1 = BC9VPC [package=bc9vpc]
  BAT2 = BC9VPC [package=bc9vpc]
  BAT3 = BC9VPC [package=bc9vpc]
  U3 = EDISON  # not connected

nets:
  GND: U1.GND, U1.IN1, U2.GND, Componente1.D7, Componente1.GND
  N1: U1.IN2, Componente1.D8_PWM/A8
  N2: U1.K1-Off, U1.K2-Off, U2.K1-Off, U2.K2-Off, BAT3.V+
  N3: U1.K1-On, U1.K2-On, U2.K1-On, U2.K2-On, BAT1.V-
  N4: U2.IN1, Componente1.D6_PWM/A7
  N5: U2.IN2, Componente1.D5_PWM
  N6: BAT1.V+, BAT2.V-
  N7: BAT2.V+, BAT3.V-

custom parts:
  2-Channel 5v Relay Shield: 2 Channel 5v Relay Shield w. 2x SPD-06VDC-SD-C
