# Fritzing sketch Fonte 5v-12v (saved by Fritzing 0.9.3b)
breadboards: 1

parts:
  U1 = Voltage Regulator - 5V [package="TO220 [THT]"]
  J1 = Screw terminal - 2 pins [package=THT]
  J2 = Screw terminal - 2 pins [package=THT]
  VCC1 = Battery
  VCC2 = Battery
  VCC3 = Battery
  VCC4 = Battery
  S1 = Toggle Switch [package=THT]

nets:
  N1: U1.input_voltage, J1.pin2, VCC3.+
  N2: U1.GND, J2.pin1, S1.L2
  N3: U1.output_voltage, J2.pin2
  N4: VCC1.-, VCC2.+
  N5: VCC1.+, VCC3.-
  N6: VCC2.-, VCC4.+
  N7: VCC4.-, S1.COM
