# Fritzing sketch SensorDeJanela (saved by Fritzing 0.9.3b)
breadboards: 2

parts:
  WeMos_D1_Mini1 = WeMos D1 Mini  # not connected
  D2F1 = D2F-FL Omron Snap Action Limit Switch with Level
  R2 = Resistor [tolerance=±2% resistance=10k package="0603 [SMD]"]

nets:
  N1: D2F1.NO, R2.Pin_1

custom parts:
  D2F-FL Omron Snap Action Limit Switch with Level: Snap action switch with stainless steel lever.
