# Fritzing sketch SensorDePassagem (saved by Fritzing 0.9.3b)
breadboards: 1

parts:
  WeMos_D1_Mini1 = WeMos D1 Mini
  hc-sr1 = hc-sr04
  hc-sr2 = hc-sr04

nets:
  N1: WeMos_D1_Mini1.D1, hc-sr1.Trig
  N2: WeMos_D1_Mini1.D2, hc-sr1.Echo
  N3: WeMos_D1_Mini1.D6, hc-sr2.Echo
  N4: WeMos_D1_Mini1.D7, hc-sr2.Trig
  VCC: hc-sr1.VCC, hc-sr2.VCC
  GND: hc-sr1.GND, hc-sr2.GND
