# Fritzing sketch SensorLuminosidade (saved by Fritzing 0.9.3b)
breadboards: 1

parts:
  R1 = PHOTOCELL [package=photocell]
  R2 = Resistor [tolerance=±5% resistance=10 package="2010 [SMD]"]
  WeMos_D1_Mini1 = WeMos D1 Mini  # not connected

nets:
  N1: R1.P$1, R2.Pin_1
